// Logisim project Basic Computer.circ as structural Verilog: 3 circuits, main circuit main
module main (
  input  in_1,
  input  in_2,
  input  in_3,
  input  in_4,
  input  in_5,
  input  in_6,
  input  CLR_Signal,
  input  in_8,
  input  CLR_Signal_2,
  input  in_10,
  input  in_11,
  input  in_12,
  input  CLR_Signal_3,
  input  CLR_Signal_4,
  output [15:0] out_15
);

  wire AC_INC, AC_LD, ADD, ALU_eout, AR_LD, Clear_AC, clock_1_out, Complement_AC, d_ff_1_q, d_ff_2_q,
       d_ff_3_q, d_ff_4_q, d_ff_5_q, DR_LD, IR_LD, Memory_LD, not_1_out, PC_INC, shift_left_AC, Store_AC,
       T3I, Transfer_DR;
  wire [2:0] MUX_Sel;
  wire [7:0] bit_extender_1_out, INPR_q;
  wire [11:0] AR_q, bit_extender_2_out, bit_extender_3_out, PC_q;
  wire [15:0] AC_q, ALU_ac_2, bit_extender_4_out, bit_extender_5_out, DR_q, IR_q, ram_1_data;

  Clock clock_1 (.out(clock_1_out));
  Bit_Extender #(.in_width(16), .out_width(8)) bit_extender_1 (.in(out_15), .out(bit_extender_1_out));
  ALU ALU (
    .AC(AC_q), .DR(DR_q), .INPR(INPR_q), .Ein(d_ff_1_q), .Circular_left_with_E(shift_left_AC),
    .Circular_right_with_E(in_5), .Complement_AC(Complement_AC), .Transfer_INP(in_4),
    .Transfer_DR(Transfer_DR), .ADD(ADD), .AND(in_1), .Eout(ALU_eout), .AC_2(ALU_ac_2));
  Bit_Extender #(.in_width(16), .out_width(12)) bit_extender_2 (.in(out_15), .out(bit_extender_2_out));
  Bit_Extender #(.in_width(16), .out_width(12)) bit_extender_3 (.in(out_15), .out(bit_extender_3_out));
  D_Flip_Flop d_ff_1 (.clk(clock_1_out), .D(ALU_eout), .Q(d_ff_1_q));  // open: Qn, preset, en, reset
  Counter #(.width(12), .max('hfff)) AR (
    .load(AR_LD), .D(bit_extender_2_out), .count(in_6), .Q(AR_q), .clk(clock_1_out), .clr(d_ff_5_q));  // open: carry
  Counter #(.width(12), .max('hfff)) PC (
    .load(in_3), .D(bit_extender_3_out), .count(PC_INC), .Q(PC_q), .clk(clock_1_out));  // open: carry, clr
  Counter #(.width(16), .max('hffff)) DR (
    .load(DR_LD), .D(out_15), .count(in_8), .Q(DR_q), .clk(clock_1_out), .clr(d_ff_3_q));  // open: carry
  Counter #(.width(16), .max('hffff)) AC (
    .load(AC_LD), .D(ALU_ac_2), .count(AC_INC), .Q(AC_q), .clk(clock_1_out), .clr(Clear_AC));  // open: carry
  Register INPR (.en(in_10), .Q(INPR_q), .clk(clock_1_out));  // open: D, clr
  Counter #(.width(16), .max('hffff)) IR (
    .load(IR_LD), .D(out_15), .count(in_11), .Q(IR_q), .clk(clock_1_out), .clr(d_ff_4_q));  // open: carry
  Counter OUTR (
    .load(in_2), .D(bit_extender_1_out), .count(in_12), .clk(clock_1_out), .clr(d_ff_2_q));  // open: Q, carry
  D_Flip_Flop d_ff_2 (.clk(clock_1_out), .D(CLR_Signal_4), .Q(d_ff_2_q));  // open: Qn, preset, en, reset
  D_Flip_Flop d_ff_3 (.clk(clock_1_out), .D(CLR_Signal_2), .Q(d_ff_3_q));  // open: Qn, preset, en, reset
  LCU lcu_1 (
    .CLK(clock_1_out), .IR(IR_q), .MUX_Sel(MUX_Sel), .AR_LD(AR_LD), .PC_INC(PC_INC), .IR_LD(IR_LD),
    .DR_LD(DR_LD), .Transfer_DR(Transfer_DR), .Complement_AC(Complement_AC), .AC_INC(AC_INC), .ADD(ADD),
    .Store_AC(Store_AC), .Clear_AC(Clear_AC), .shift_left_AC(shift_left_AC), .T3I(T3I));  // open: Halt
  not not_1 (not_1_out, clock_1_out);
  D_Flip_Flop d_ff_4 (.clk(clock_1_out), .D(CLR_Signal_3), .Q(d_ff_4_q));  // open: Qn, preset, en, reset
  RAM #(.addrWidth(12), .dataWidth(16), .bus("separate")) ram_1 (
    .addr(AR_q), .din(out_15), .data(ram_1_data), .str(Store_AC), .clk(not_1_out), .ld(Memory_LD));  // open: sel, clr
  D_Flip_Flop d_ff_5 (.clk(clock_1_out), .D(CLR_Signal), .Q(d_ff_5_q));  // open: Qn, preset, en, reset
  assign bit_extender_4_out = {{4{1'b0}}, AR_q};  // Bit_Extender bit_extender_4
  assign bit_extender_5_out = {{4{1'b0}}, PC_q};  // Bit_Extender bit_extender_5
  Multiplexer #(.select(3), .width(16), .enable("false")) multiplexer_1 (
    .in1(bit_extender_4_out), .in2(bit_extender_5_out), .in3(DR_q), .in4(AC_q), .in5(IR_q), .in7(ram_1_data),
    .out(out_15), .sel(MUX_Sel));  // open: in0, in6
  or or_1 (Memory_LD, IR_LD, T3I, DR_LD);
  or or_2 (AC_LD, shift_left_AC, Complement_AC, Transfer_DR, ADD);
endmodule

module ALU (
  input  AND,
  input  ADD,
  input  Transfer_DR,
  input  Transfer_INP,
  input  Complement_AC,
  input  Circular_right_with_E,
  input  Circular_left_with_E,
  input  [15:0] AC,
  input  [15:0] DR,
  input  [7:0] INPR,
  input  Ein,
  output [15:0] AC_2,
  output Eout
);

  wire adder_1_cout, not_2_out;
  wire [1:0] bit_extender_1_out, or_1_out;
  wire [2:0] priority_encoder_1_out;
  wire [15:0] adder_1_out, and_1_out, bit_extender_2_out, not_1_out;

  Priority_Encoder priority_encoder_1 (
    .in0(AND), .in1(ADD), .in2(Transfer_DR), .in3(Transfer_INP), .in4(Complement_AC),
    .in5(Circular_right_with_E), .in6(Circular_left_with_E), .out(priority_encoder_1_out));  // open: in7, en_in, gs, en_out
  assign and_1_out = AC & DR;  // AND_Gate and_1, 16 bits wide
  assign bit_extender_1_out = {{1{ADD}}, ADD};  // Bit_Extender bit_extender_1
  Adder #(.width(16)) adder_1 (.a(AC), .b(DR), .out(adder_1_out), .cout(adder_1_cout));  // open: cin
  assign bit_extender_2_out = {{8{1'b0}}, INPR};  // Bit_Extender bit_extender_2
  Multiplexer #(.select(3), .width(16), .enable("false")) multiplexer_1 (
    .in0(and_1_out), .in1(adder_1_out), .in2(DR), .in3(bit_extender_2_out), .in4(not_1_out),
    .in5({Ein, AC[15:1]}), .in6({AC[14:0], Ein}), .out(AC_2), .sel(priority_encoder_1_out));  // open: in7
  assign not_1_out = ~AC;  // NOT_Gate not_1, 16 bits wide
  assign or_1_out = bit_extender_1_out | {Circular_left_with_E, Circular_right_with_E};  // OR_Gate or_1, 2 bits wide
  Multiplexer #(.select(2), .disabled(0), .enable("false")) multiplexer_2 (
    .in0(not_2_out), .in1(AC[0]), .in2(AC[15]), .in3(adder_1_cout), .out(Eout), .sel(or_1_out));
  not not_2 (not_2_out, 1'b1);
endmodule

module LCU (
  input  [15:0] IR,
  input  CLK,
  output [2:0] MUX_Sel,
  output AR_LD,
  output PC_INC,
  output IR_LD,
  output DR_LD,
  output Transfer_DR,
  output Complement_AC,
  output AC_INC,
  output ADD,
  output Store_AC,
  output Clear_AC,
  output shift_left_AC,
  output Halt,
  output T3I
);

  wire and_1_out, and_2_out, and_3_out, and_4_out, and_6_out, and_7_out, and_8_out, B0, B1, B2, B3, B4, B5,
       B6, B7, B8, B9, B10, B11, Clear, D0, D1, D1T4, D2, D2T4, D2T6, D3, D4, D5, D6, D7, d_ff_1_q, d_ff_2_q,
       I, I_prime, not_2_out, or_4_out, r, S_q, Stop, T0, T2, T3, T4, T5, T6, T7;
  wire [2:0] bitselector_2_out;
  wire [3:0] SC_q;
  wire [11:0] IR11;

  not not_1 (I_prime, I);
  and and_1 (and_1_out, T3, D7, I_prime, B11);
  BitSelector #(.width(16)) bitselector_1 (.in(IR), .out(I), .sel(4'b1111));
  Decoder #(.select(4), .enable("false")) decoder_1 (
    .out0(T0), .out1(IR_LD), .out2(T2), .out3(T3), .out4(T4), .out5(T5), .out6(T6), .out7(T7), .sel(SC_q));  // open: out8, out9, out10, out11, out12, out13, out14, out15
  D_Flip_Flop S (.clk(CLK), .Q(S_q), .preset(1'b1), .en(1'b1), .reset(d_ff_1_q));  // open: D, Qn
  D_Flip_Flop d_ff_1 (.clk(Halt), .D(1'b1), .Q(d_ff_1_q));  // open: Qn, preset, en, reset
  and and_2 (and_2_out, T3, D7, I_prime, B9);
  BitSelector #(.width(16), .group(3)) bitselector_2 (.in(IR), .out(bitselector_2_out), .sel(3'b100));
  Decoder #(.select(3), .enable("false")) decoder_2 (
    .out0(D0), .out1(D1), .out2(D2), .out3(D3), .out4(D4), .out5(D5), .out6(D6), .out7(D7),
    .sel(bitselector_2_out));
  or or_1 (Clear, and_1_out, and_2_out, and_3_out, T5, and_4_out, and_6_out, and_7_out);
  and and_3 (and_3_out, T5, D3);
  Counter #(.width(4), .max('hf)) SC (.count(S_q), .Q(SC_q), .clk(CLK), .clr(d_ff_2_q));  // open: load, D, carry
  D_Flip_Flop d_ff_2 (.clk(CLK), .D(Clear), .Q(d_ff_2_q));  // open: Qn, preset, en, reset
  and and_4 (and_4_out, T3, D7, I_prime, B5);
  BitSelector #(.width(16), .group(12)) bitselector_3 (.in(IR), .out(IR11), .sel(1'b0));
  and and_5 (Stop, IR[0], IR[13], IR[14], IR[12]);
  and and_6 (and_6_out, T3, D7, I_prime, B0);
  and and_7 (and_7_out, T3, D7, I_prime, B6);
  and ADD1 (D1T4, D1, T4);
  and LDA1 (D2T4, D2, T4);
  BitSelector #(.width(12)) bitselector_4 (.in(IR11), .out(B0), .sel(4'b0000));
  BitSelector #(.width(12)) bitselector_5 (.in(IR11), .out(B1), .sel(4'b0001));
  BitSelector #(.width(12)) bitselector_6 (.in(IR11), .out(B2), .sel(4'b0010));
  BitSelector #(.width(12)) bitselector_7 (.in(IR11), .out(B3), .sel(4'b0011));
  BitSelector #(.width(12)) bitselector_8 (.in(IR11), .out(B4), .sel(4'b0100));
  BitSelector #(.width(12)) bitselector_9 (.in(IR11), .out(B5), .sel(4'b0101));
  BitSelector #(.width(12)) bitselector_10 (.in(IR11), .out(B6), .sel(4'b0110));
  BitSelector #(.width(12)) bitselector_11 (.in(IR11), .out(B7), .sel(4'b0111));
  BitSelector #(.width(12)) bitselector_12 (.in(IR11), .out(B8), .sel(4'b1000));
  BitSelector #(.width(12)) bitselector_13 (.in(IR11), .out(B9), .sel(4'b1001));
  BitSelector #(.width(12)) bitselector_14 (.in(IR11), .out(B10), .sel(4'b1010));
  BitSelector #(.width(12)) bitselector_15 (.in(IR11), .out(B11), .sel(4'b1011));
  not not_2 (not_2_out, Stop);
  and and_8 (and_8_out, not_2_out, T0);
  and and_9 (D2T6, D2, T6);
  and and_10 (r, T3, I_prime, D7);
  or or_2 (AR_LD, and_8_out, T3I, T2);
  or or_3 (DR_LD, D1T4, D2T4);
  and ADD2 (ADD, D1, T5);
  and STA (Store_AC, D3, T4);
  and LDA2 (Transfer_DR, D2, T5);
  and CMA (Complement_AC, r, B9);
  and INC (AC_INC, r, B5);
  and and_11 (T3I, T3, I);
  and CLA (Clear_AC, r, B11);
  and CIL (shift_left_AC, r, B6);
  and HLT (Halt, r, B0);
  assign MUX_Sel = 1'b0 ? 3'b000 : 3'bz;  // Controlled_Buffer controlled_buffer_1
  assign MUX_Sel = 1'b0 ? 3'b001 : 3'bz;  // Controlled_Buffer controlled_buffer_2
  assign MUX_Sel = T0 ? 3'b010 : 3'bz;  // Controlled_Buffer controlled_buffer_3
  assign MUX_Sel = 1'b0 ? 3'b011 : 3'bz;  // Controlled_Buffer controlled_buffer_4
  assign MUX_Sel = Store_AC ? 3'b100 : 3'bz;  // Controlled_Buffer controlled_buffer_5
  assign MUX_Sel = T2 ? 3'b101 : 3'bz;  // Controlled_Buffer controlled_buffer_6
  assign MUX_Sel = 1'b0 ? 3'b110 : 3'bz;  // Controlled_Buffer controlled_buffer_7
  assign MUX_Sel = or_4_out ? 3'b111 : 3'bz;  // Controlled_Buffer controlled_buffer_8
  or or_4 (or_4_out, IR_LD, DR_LD, T3I);

  assign PC_INC = IR_LD;

  // Other names for the same wires on the sheet: D1T5 = ADD; D3T4 = Store_AC; HLT = Halt; rB5 = AC_INC;
  //   rB9 = Complement_AC; T1 = IR_LD
endmodule
